# Fritzing sketch FINAL_Breadboard (saved by Fritzing 0.9.4)
breadboards: 1

parts:
  Raspberry_Pi_1 = Raspberry Pi 4 [part_number=RPI-4-b]
  OLED = Grove OLED 128x96
  DS1 = DS18B20 1-Wire Temperature Sensor [part_number=DS18B20]
  R1 = Resistor [tolerance=±5% resistance=4.7k package="2010 [SMD]"]
  Part1 = Adafruit ADS1115 16Bit I2C ADC [part_number="Adafruit #1085"]
  R3 = PHOTOCELL [package=photocell-kit]
  R4 = Resistor [tolerance=±5% resistance=10k package="2010 [SMD]"]
  ADC1 = MCP3008 [package=dil16]
  Mod1 = generic-ac-power-supply [package=THT]
  M2 = ph-4502c [package=THT]

nets:
  VDD: Raspberry_Pi_1.3v3, OLED.VCC, DS1.VDD, R1.Pin_0, Part1.VDD, R3.P$2, ADC1.VREF, ADC1.VDD, Mod1.pin3#2
  N1: Raspberry_Pi_1.GPIO2, OLED.SDA, Part1.SDA
  N2: Raspberry_Pi_1.GPIO3, OLED.SCL, Part1.SCL
  GND: Raspberry_Pi_1.GND, OLED.GND, DS1.GND, Part1.GND, R4.Pin_0, ADC1.CH5, ADC1.DGND, ADC1.AGND, Mod1.pin3#3, M2.pin4, M2.pin5
  N3: Raspberry_Pi_1.GPIO6, ADC1.CLK
  N4: Raspberry_Pi_1.GPIO13, ADC1.Dout
  N5: Raspberry_Pi_1.GPIO19, ADC1.Din
  N6: Raspberry_Pi_1.GPIO26, ADC1.CS/SHDN
  N7: Raspberry_Pi_1.GPIO21, DS1.DQ, R1.Pin_1
  N8: Raspberry_Pi_1.5V, M2.pin6
  N9: Part1.AIN0, M2.pin3
  N10: R3.P$1, R4.Pin_1, ADC1.CH0

custom parts:
  Raspberry Pi 4: The RPi4, a faster version of the awesome Raspberry Pi 2 B ARM Board with 40 pin gpio. Ready for special Raspberry Pi B+ and RPi2 Hat (Hardware attached (on) top)
  Adafruit ADS1115 16Bit I2C ADC: For microcontrollers without an analog-to-digital converter or when you want a higher-precision ADC, the ADS1115 provides 16-bit precision at 860 samples/second over I2C. The chip can be configured as 4 single-ended input channels, or two differential channels. As a nice bonus, it even includes a programmable gain amplifier, up to x16, to help boost up smaller single/differential signals to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
  generic-ac-power-supply: Generic ac power supply module. Use as is, or customize the svgs to fit your particular device (as they are all different.) Provides AC input and single DC output. PCB is generic and will need modifications if you intend to do a pcb mount.
  ph-4502c: ph-4502c PH Meter.
